// Logisim project XORFromAndsORsNOTs01.circ as structural Verilog: 1 circuit, main circuit main
module main (
  input  In1,
  input  In2,
  output XOR
);

  wire and_1_out, and_2_out, not_1_out, not_2_out;

  not not_1 (not_1_out, In1);
  not not_2 (not_2_out, In2);
  and and_1 (and_1_out, not_1_out, not_1_out, In2);
  and and_2 (and_2_out, In1, not_2_out);
  or or_1 (XOR, and_1_out, and_2_out);

  // Notes on the sheet:
  //   XOR from Combination of ORs, ANDs, and NOTs
endmodule
